# Fritzing sketch Safety Printer (saved by Fritzing 0.9.6b)
perfboards: 1

parts:
  MCU = Arduino Nano (Rev3.0)
  R4 = Resistor [tolerance=±5% power=0.25 resistance=470 package=THT]
  R5 = Resistor [tolerance=±5% power=0.25 resistance=1000 package=THT]
  Flame_Sensor_2 = JST-03JQ-BT [part_number=C3 package=THT]
  Alarm_LED = LEDs [package=led10mm]
  Reset_Switch = Pushbutton [package="[SMD]"]
  R3 = Resistor [tolerance=±5% power=0.25 resistance=470 package=THT]
  Flame_Sensor_1 = JST-03JQ-BT [part_number=C2 package=THT]
  Interlock_Relay = JST-03JQ-BT [part_number=C5 package=THT]
  R2 = Resistor [tolerance=±5% power=0.25 resistance=1000 package=THT]
  Trip_LED = LEDs [package=led10mm]
  R1 = Resistor [tolerance=±5% power=0.25 resistance=1000 package=THT]
  Smoke_Sensor = Header 2 [part_number=C1 package=jst-2-smd]
  part = Header 2 [package=jst-2-smd]
  Emergency_Button = Screw terminal - 2 pins [part_number=C4 package=THT]
  Step_Up_Buck_Converter = RioRand LM2596 [part_number=MT3608]
  Bed_temperature_NTC_Thermistor = Header 2 [part_number=C6 package=jst-2-pth-kit]
  R6 = Resistor [tolerance=±5% power=0.25 resistance=4.7k package=THT]
  Hot_end_temperature_NTC_Thermistor = Header 2 [part_number=C7 package=jst-2-pth-kit]
  R7 = Resistor [tolerance=±5% power=0.25 resistance=4.7k package=THT]
  Optional_I2C_LCD_16x2 = polarizedheader 4pin 0.156in [package=THT]

nets:
  N1: MCU.GND, R4.Pin_1, R5.Pin_1, Flame_Sensor_2.pin2, R3.Pin_1, Flame_Sensor_1.pin2, Interlock_Relay.pin2, R2.Pin_1, R1.Pin_1, Step_Up_Buck_Converter.Pin_2, Bed_temperature_NTC_Thermistor.1, Hot_end_temperature_NTC_Thermistor.1, Optional_I2C_LCD_16x2.pin2
  N2: MCU.D2, R7.Pin_0
  N3: MCU.D3, R6.Pin_0
  N4: MCU.D5, R2.Pin_0, Emergency_Button.pin2
  N5: MCU.D6, Interlock_Relay.pin3
  N6: MCU.D7, R1.Pin_0, part.2
  N7: MCU.D8, Flame_Sensor_2.pin1
  N8: MCU.D9, Flame_Sensor_1.pin1
  N9: MCU.D10, Alarm_LED.A
  N10: MCU.D11/MOSI, Reset_Switch.Pin_3
  N11: MCU.D12/MISO, Trip_LED.A
  N12: MCU.5V, Flame_Sensor_2.pin3, Flame_Sensor_1.pin3, Interlock_Relay.pin1, part.1, Emergency_Button.pin1, Step_Up_Buck_Converter.Pin_1, Optional_I2C_LCD_16x2.pin1
  N13: MCU.A7, Bed_temperature_NTC_Thermistor.2, R6.Pin_1
  N14: MCU.A6, Hot_end_temperature_NTC_Thermistor.2, R7.Pin_1
  N15: MCU.A5, Optional_I2C_LCD_16x2.pin4
  N16: MCU.A4, Optional_I2C_LCD_16x2.pin3
  N17: R4.Pin_0, Trip_LED.C
  N18: R5.Pin_0, Reset_Switch.Pin_1, Reset_Switch.Pin_2
  N19: Alarm_LED.C, R3.Pin_0
  N20: Smoke_Sensor.2, Step_Up_Buck_Converter.Pin_4
  N21: Smoke_Sensor.1, Step_Up_Buck_Converter.Pin_3

notes:
  5 Vcc
  GND
  SDA
  SCL
  12 Vcc
  signal -
  signal +
  signal
